# Fritzing sketch StoveServoController (saved by Fritzing 0.9.4)
circuit board: 8.46667cm x 5.64444cm
breadboards: 1

parts:
  Particle = Particle Xenon
  TempProbe = Adafruit Thermocouple Amplifier with 1-Wire Breakout Board - MAX31850K [part_number="Adafruit #1727"]
  Servo = female pin header, 3 pins [form="♀ (female)"]
  Buzzer = Piezo Speaker
  LED = LED - 5mm [color="Red (633nm)" package="5 mm [THT]"]
  Button = Pushbutton [package=THT]
  R1 = Resistor [tolerance=±5% resistance=220 package=THT]

nets:
  3.3V: Particle.3.3V, TempProbe.VIN, R1.Pin_1
  GND: Particle.GND, TempProbe.GND, Servo.pin1, Buzzer.pin1, LED.anode, Button.leg1
  N1: Particle.A0, LED.cathode
  N2: Particle.A1, Buzzer.pin2
  N3: Particle.A4, Button.leg0
  N4: Particle.D2, Servo.pin3
  N5: Particle.D3, TempProbe.DATA, R1.Pin_0
  N6: Particle.VUSB, Servo.pin2

custom parts:
  Particle Xenon: The Boron LTE is a powerful LTE CAT-M1 enabled development kit that can act as either a standalone cellular device or LTE enabled gateway, repeater, or endpoint for a Particle Mesh networks. Equipped with the Nordic nRF52840 and u-blox SARA 410 processors, the Boron has built-in battery charging circuitry which makes it easier to connect a Li-Po battery and 20 mixed signal GPIOs to interface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
  Adafruit Thermocouple Amplifier with 1-Wire Breakout Board - MAX31850K: Thermocouples are very sensitive, requiring a good amplifier with a cold-compensation reference. So far we've carried the very nice MAX31855 which is an SPI interface thermocouple amplifier. The '855 is great but if you have a lot of thermocouples to measure it isn't terribly easy to use. That's why we are also carrying the new '850 model from Maxim - it's a "1-Wire" thermocouple amp which can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
